// Logisim project 单周期CPU.circ as structural Verilog
module main (
  input  rst
);

  wire _1, ALUsrc, clk, Extop, J, MemtoReg, MenWr, NPC_sel, or_1_out, or_2_out, or_3_out, RegDst, RegWr, zero;
  wire [1:0] ALUctr;
  wire [4:0] multiplexer_1_out, rd, rs, rt, shamt;
  wire [5:0] funct, opcode;
  wire [15:0] IMM16;
  wire [25:0] address;
  wire [31:0] multiplexer_2_out, multiplexer_3_out, \取指令单元_1_out_6 , \扩展单元_1_data_out , \数据存储器_1_data_out ,
       \算术逻辑单元_1_aluout , \通用寄存器组_1_data_out_rs , \通用寄存器组_1_data_out_rt ;

  Multiplexer #(.width(5), .enable("false")) multiplexer_1 (.in0(rt), .in1(rd), .out(multiplexer_1_out), .sel(RegDst));
  Clock u_clk (.out(clk));
  \通用寄存器组  \u_通用寄存器组_1  (
    .address_rs(rs), .data_out_rs(\通用寄存器组_1_data_out_rs ), .data_in(multiplexer_3_out), .GPR_CLK(clk),
    .clear(rst), .data_out_rt(\通用寄存器组_1_data_out_rt ), .address_rt(rt), .address_w(multiplexer_1_out),
    .in_7(RegWr));
  \扩展单元  \u_扩展单元_1  (.data_in(IMM16), .Extop(Extop), .data_out(\扩展单元_1_data_out ));
  or or_1 (or_1_out, NPC_sel, J);
  or or_2 (or_2_out, J, zero);
  Multiplexer #(.width(32), .enable("false")) multiplexer_2 (
    .in0(\通用寄存器组_1_data_out_rt ), .in1(\扩展单元_1_data_out ), .out(multiplexer_2_out), .sel(ALUsrc));
  \取指令单元  \u_取指令单元_1  (.NPCsel(or_1_out), .zero(or_2_out), .clock(clk), .rst(rst), .out_6(\取指令单元_1_out_6 ), .J(J));
  \分线器  \u_分线器_1  (
    .in_1(\取指令单元_1_out_6 ), .OPCODE(opcode), .RS(rs), .RT(rt), .RD(rd), .SHAMT(shamt), .FUNCT(funct),
    .IMM(IMM16), .ADDRRSS(address));
  \算术逻辑单元  \u_算术逻辑单元_1  (
    .A(\通用寄存器组_1_data_out_rs ), .B(multiplexer_2_out), .ALU_ctr(ALUctr),
    .ALUout({\算术逻辑单元_1_aluout [31:17], _1, \算术逻辑单元_1_aluout [15:0]}));
  \数据存储器  \u_数据存储器_1  (
    .address(\算术逻辑单元_1_aluout [9:2]), .data_in(\通用寄存器组_1_data_out_rt ), .clk(clk), .clear(rst),
    .data_out(\数据存储器_1_data_out ), .MenWr(MenWr));
  Multiplexer #(.width(32), .enable("false")) multiplexer_3 (
    .in0({\算术逻辑单元_1_aluout [31:17], _1, \算术逻辑单元_1_aluout [15:0]}), .in1(\数据存储器_1_data_out ),
    .out(multiplexer_3_out), .sel(MemtoReg));
  \控制器  \u_控制器_1  (
    .opcode(opcode), .funct(funct), .out_3(RegDst), .out_4(ALUsrc), .out_5(MemtoReg), .out_6(RegWr),
    .out_7(MenWr), ._5_7(NPC_sel), ._3_4_6(Extop), .out_10(ALUctr), .J_sel(J));
  not not_1 (zero, or_3_out);
  or or_3 (or_3_out, \算术逻辑单元_1_aluout [0], \算术逻辑单元_1_aluout [1], \算术逻辑单元_1_aluout [2], \算术逻辑单元_1_aluout [3], \算术逻辑单元_1_aluout [4], \算术逻辑单元_1_aluout [5], \算术逻辑单元_1_aluout [6], \算术逻辑单元_1_aluout [7], \算术逻辑单元_1_aluout [8], \算术逻辑单元_1_aluout [9], \算术逻辑单元_1_aluout [10], \算术逻辑单元_1_aluout [11], \算术逻辑单元_1_aluout [12], \算术逻辑单元_1_aluout [13], \算术逻辑单元_1_aluout [14], \算术逻辑单元_1_aluout [15], \算术逻辑单元_1_aluout [17], \算术逻辑单元_1_aluout [18], \算术逻辑单元_1_aluout [19], \算术逻辑单元_1_aluout [20], \算术逻辑单元_1_aluout [21], \算术逻辑单元_1_aluout [22], \算术逻辑单元_1_aluout [23], \算术逻辑单元_1_aluout [24], \算术逻辑单元_1_aluout [25], \算术逻辑单元_1_aluout [26], \算术逻辑单元_1_aluout [27], \算术逻辑单元_1_aluout [28], \算术逻辑单元_1_aluout [29], \算术逻辑单元_1_aluout [30], \算术逻辑单元_1_aluout [31], _1);

  // Notes on the sheet:
  //   判断结果是否为0
endmodule

// controller
module \控制器  (
  input  [5:0] opcode,
  input  [5:0] funct,
  output out_3,
  output out_4,
  output out_5,
  output out_6,
  output out_7,
  output _5_7,
  output _3_4_6,
  output [1:0] out_10,
  output J_sel
);

  wire _0, ADD_out, not_1_out, not_3_out, not_5_out, or_2_out, or_3_out, or_4_out, or_5_out, or_6_out,
       or_7_out, or_8_out, or_9_out, or_10_out, OR_11_out, shift_out;
  wire [5:0] in, subtractor_1_out, subtractor_2_out, subtractor_3_out, subtractor_4_out, subtractor_5_out,
       subtractor_6_out, subtractor_7_out, subtractor_8_out;
  wire [6:0] not_2_out;

  or or_1 (_0, opcode[0], opcode[1], opcode[2], opcode[3], opcode[4], opcode[5]);
  Multiplexer #(.width(6), .enable("false")) multiplexer_1 (.in0(opcode), .in1(funct), .out(in), .sel(not_1_out));
  not not_1 (not_1_out, _0);
  Subtractor #(.width(6)) subtractor_1 (.a(in), .b(6'b100001), .out(subtractor_1_out));  // open: bin, bout
  Subtractor #(.width(6)) subtractor_2 (.a(in), .b(6'b100011), .out(subtractor_2_out));  // open: bin, bout
  Subtractor #(.width(6)) subtractor_3 (.a(in), .b(6'b001101), .out(subtractor_3_out));  // open: bin, bout
  Subtractor #(.width(6)) subtractor_4 (.a(in), .b(6'b100011), .out(subtractor_4_out));  // open: bin, bout
  Subtractor #(.width(6)) subtractor_5 (.a(in), .b(6'b101011), .out(subtractor_5_out));  // open: bin, bout
  Subtractor #(.width(6)) subtractor_6 (.a(in), .b(6'b000100), .out(subtractor_6_out));  // open: bin, bout
  Subtractor #(.width(6)) subtractor_7 (.a(in), .b(6'b001111), .out(subtractor_7_out));  // open: bin, bout
  Subtractor #(.width(6)) subtractor_8 (.a(in), .b(6'b000010), .out(subtractor_8_out));  // open: bin, bout
  not not_2 (not_2_out[0], or_2_out);
  or or_2 (or_2_out, subtractor_1_out[0], subtractor_1_out[1], subtractor_1_out[2], subtractor_1_out[3], subtractor_1_out[4], subtractor_1_out[5]);
  or or_3 (or_3_out, subtractor_2_out[0], subtractor_2_out[1], subtractor_2_out[2], subtractor_2_out[3], subtractor_2_out[4], subtractor_2_out[5]);
  not not_3 (not_3_out, or_3_out);
  not not_4 (not_2_out[2], or_4_out);
  or or_4 (or_4_out, subtractor_3_out[0], subtractor_3_out[1], subtractor_3_out[2], subtractor_3_out[3], subtractor_3_out[4], subtractor_3_out[5]);
  or or_5 (or_5_out, subtractor_4_out[0], subtractor_4_out[1], subtractor_4_out[2], subtractor_4_out[3], subtractor_4_out[4], subtractor_4_out[5]);
  not not_5 (not_5_out, or_5_out);
  not not_6 (not_2_out[4], or_6_out);
  or or_6 (or_6_out, subtractor_5_out[0], subtractor_5_out[1], subtractor_5_out[2], subtractor_5_out[3], subtractor_5_out[4], subtractor_5_out[5]);
  or or_7 (or_7_out, subtractor_6_out[0], subtractor_6_out[1], subtractor_6_out[2], subtractor_6_out[3], subtractor_6_out[4], subtractor_6_out[5]);
  not not_7 (not_2_out[5], or_7_out);
  not not_8 (not_2_out[6], or_8_out);
  or or_8 (or_8_out, subtractor_7_out[0], subtractor_7_out[1], subtractor_7_out[2], subtractor_7_out[3], subtractor_7_out[4], subtractor_7_out[5]);
  or or_9 (or_9_out, subtractor_8_out[0], subtractor_8_out[1], subtractor_8_out[2], subtractor_8_out[3], subtractor_8_out[4], subtractor_8_out[5]);
  not not_9 (J_sel, or_9_out);
  Multiplexer #(.enable("false")) multiplexer_2 (.in0(not_3_out), .in1(1'b0), .out(not_2_out[1]), .sel(_0));
  Multiplexer #(.enable("false")) multiplexer_3 (.in0(1'b0), .in1(not_5_out), .out(not_2_out[3]), .sel(_0));
  or ADD (ADD_out, not_2_out[0], not_2_out[3], not_2_out[4]);
  or or_10 (or_10_out, not_2_out[5], not_2_out[1]);
  buf OR_11 (OR_11_out, not_2_out[2]);
  buf shift (shift_out, not_2_out[6]);
  or RegDst (out_3, not_2_out[0], not_2_out[1]);
  or Alusrc (out_4, not_2_out[2], not_2_out[3], not_2_out[4], not_2_out[6]);
  buf Mem2Reg (out_5, not_2_out[3]);
  or Regwrite (out_6, not_2_out[0], not_2_out[1], not_2_out[2], not_2_out[3], not_2_out[6]);
  buf MemWrite (out_7, not_2_out[4]);
  buf buffer_1 (_5_7, not_2_out[5]);
  or Extop (_3_4_6, not_2_out[3], not_2_out[4], not_2_out[2], not_2_out[6]);
  Priority_Encoder #(.select(2)) priority_encoder_1 (
    .in0(ADD_out), .in1(or_10_out), .in2(OR_11_out), .in3(shift_out), .out(out_10));  // open: gs, en_out, en_in

  // Notes on the sheet:
  //   addu
  //   ori
  //   lw
  //   sw
  //   beq
  //   lui
  //   j
  //   subu
  //   0 3 4
  //   1
  //   2
  //   6
  //   0 1
  //   2 3 4 6
  //   3
  //   0 1 2 3 6
  //    4
endmodule

// IFU
module \取指令单元  (
  input  NPCsel,
  input  zero,
  input  clock,
  input  rst,
  input  J,
  output [31:0] out_6
);

  wire and_1_out;
  wire [27:0] adder_1_out;
  wire [31:0] adder_2_out, bit_extender_1_out, multiplexer_1_out, multiplexer_2_out, multiplexer_3_out, PC_q,
       shifter_1_out;
  wire [31:28] newPC;

  assign bit_extender_1_out = {{16{out_6[15]}}, out_6[15:0]};  // Bit_Extender bit_extender_1
  Shifter #(.width(32)) shifter_1 (.in(bit_extender_1_out), .\dist (5'b00010), .out(shifter_1_out));
  Adder #(.width(32)) adder_1 (.a(PC_q), .b(32'h4), .out({newPC, adder_1_out}));  // open: cin, cout
  Adder #(.width(32)) adder_2 (.a({newPC, adder_1_out}), .b(shifter_1_out), .out(adder_2_out));  // open: cin, cout
  and and_1 (and_1_out, NPCsel, zero);
  Multiplexer #(.width(32), .enable("false")) multiplexer_1 (
    .in0({newPC, adder_1_out}), .in1(adder_2_out), .out(multiplexer_1_out), .sel(and_1_out));
  Multiplexer #(.width(32), .enable("false")) multiplexer_2 (
    .in0(multiplexer_3_out), .in1(32'h3000), .out(multiplexer_2_out), .sel(rst));
  Multiplexer #(.width(32), .enable("false")) multiplexer_3 (
    .in0(multiplexer_1_out), .in1({newPC, out_6[25:0], 2'b00}), .out(multiplexer_3_out), .sel(J));
  Register #(.width(32)) PC (.D(multiplexer_2_out), .Q(PC_q), .clk(clock));  // open: en, clr
  ROM rom_1 (.addr(PC_q[9:2]), .data(out_6[31:24]));  // open: sel
  ROM rom_2 (.addr(PC_q[9:2]), .data(out_6[23:16]));  // open: sel
  ROM rom_3 (.addr(PC_q[9:2]), .data(out_6[15:8]));  // open: sel
  ROM rom_4 (.addr(PC_q[9:2]), .data(out_6[7:0]));  // open: sel
  // Probe on out_6

  // Other names for the same wires on the sheet: IMM[15:0] = out_6[15:0]; newPC[27:2] = out_6[25:0];
  //   PC_4_31_28[3:0] = newPC

  // Notes on the sheet:
  //   contents of rom_1 (hex, n*v repeats v):
  //   3c 35 34 34 1 1 ad 8d 1 11 8 9*1
  //   contents of rom_2 (hex, n*v repeats v):
  //   8 8 9 a 4a 69 b c 2a 20 10 9*4a
  //   contents of rom_3 (hex, n*v repeats v):
  //   10 0 0 0 58 58 0 0 48 0 0 9*58
  //   contents of rom_4 (hex, n*v repeats v):
  //   0 4 5 1 21 23 0 0 23 1 4 9*21
endmodule

// GPR
module \通用寄存器组  (
  input  [4:0] address_rs,
  input  [4:0] address_rt,
  input  [31:0] data_in,
  input  [4:0] address_w,
  input  GPR_CLK,
  input  clear,
  input  in_7,
  output [31:0] data_out_rs,
  output [31:0] data_out_rt
);

  wire _0, _1, _2, _3, _4, _5, _6, _7, _8, _9, _10, _11, _12, _13, _14, _15, _16, _17, _18, _19, _20, _21,
       _22, _23, _24, _25, _26, _27, _28, _29, _30, _31;
  wire [31:0] r0, r1, r2, r3, r4, r5, r6, r7, r8, r9, r10, r11, r12, r13, r14, r15, r16, r17, r18, r19, r20,
       r21, r22, r23, r24, r25, r26, r27, r28, r29, r30, r31, w0, w1, w2, w3, w4, w5, w6, w7, w8, w9, w10,
       w11, w12, w13, w14, w15, w16, w17, w18, w19, w20, w21, w22, w23, w24, w25, w26, w27, w28, w29, w30,
       w31;

  Register #(.width(32)) reg0 (.D(w0), .en(_0), .Q(r0), .clk(GPR_CLK), .clr(clear));
  Register #(.width(32)) reg4 (.D(w4), .en(_4), .Q(r4), .clk(GPR_CLK), .clr(clear));
  Register #(.width(32)) reg8 (.D(w8), .en(_8), .Q(r8), .clk(GPR_CLK), .clr(clear));
  Register #(.width(32)) reg12 (.D(w12), .en(_12), .Q(r12), .clk(GPR_CLK), .clr(clear));
  Multiplexer #(.select(5), .width(32), .enable("false")) multiplexer_1 (
    .in0(r0), .in1(r1), .in2(r2), .in3(r3), .in4(r4), .in5(r5), .in6(r6), .in7(r7), .in8(r8), .in9(r9),
    .in10(r10), .in11(r11), .in12(r12), .in13(r13), .in14(r14), .in15(r15), .in16(r16), .in17(r17),
    .in18(r18), .in19(r19), .in20(r20), .in21(r21), .in22(r22), .in23(r23), .in24(r24), .in25(r25),
    .in26(r26), .in27(r27), .in28(r28), .in29(r29), .in30(r30), .in31(r31), .out(data_out_rs),
    .sel(address_rs));
  Multiplexer #(.select(5), .width(32), .enable("false")) multiplexer_2 (
    .in0(r0), .in1(r1), .in2(r2), .in3(r3), .in4(r4), .in5(r5), .in6(r6), .in7(r7), .in8(r8), .in9(r9),
    .in10(r10), .in11(r11), .in12(r12), .in13(r13), .in14(r14), .in15(r15), .in16(r16), .in17(r17),
    .in18(r18), .in19(r19), .in20(r20), .in21(r21), .in22(r22), .in23(r23), .in24(r24), .in25(r25),
    .in26(r26), .in27(r27), .in28(r28), .in29(r29), .in30(r30), .in31(r31), .out(data_out_rt),
    .sel(address_rt));
  Register #(.width(32)) reg1 (.D(w1), .en(_1), .Q(r1), .clk(GPR_CLK), .clr(clear));
  Register #(.width(32)) reg5 (.D(w5), .en(_5), .Q(r5), .clk(GPR_CLK), .clr(clear));
  Register #(.width(32)) rerg9 (.D(w9), .en(_9), .Q(r9), .clk(GPR_CLK), .clr(clear));
  Register #(.width(32)) reg13 (.D(w13), .en(_13), .Q(r13), .clk(GPR_CLK), .clr(clear));
  Register #(.width(32)) reg2 (.D(w2), .en(_2), .Q(r2), .clk(GPR_CLK), .clr(clear));
  Register #(.width(32)) reg6 (.D(w6), .en(_6), .Q(r6), .clk(GPR_CLK), .clr(clear));
  Register #(.width(32)) reg10 (.D(w10), .en(_10), .Q(r10), .clk(GPR_CLK), .clr(clear));
  Register #(.width(32)) reg14 (.D(w14), .en(_14), .Q(r14), .clk(GPR_CLK), .clr(clear));
  Demultiplexer #(.select(5), .width(32), .enable("false")) demultiplexer_1 (
    .out0(w0), .out1(w1), .out2(w2), .out3(w3), .out4(w4), .out5(w5), .out6(w6), .out7(w7), .out8(w8),
    .out9(w9), .out10(w10), .out11(w11), .out12(w12), .out13(w13), .out14(w14), .out15(w15), .out16(w16),
    .out17(w17), .out18(w18), .out19(w19), .out20(w20), .out21(w21), .out22(w22), .out23(w23), .out24(w24),
    .out25(w25), .out26(w26), .out27(w27), .out28(w28), .out29(w29), .out30(w30), .out31(w31), .in(data_in),
    .sel(address_w));
  Register #(.width(32)) reg3 (.D(w3), .en(_3), .Q(r3), .clk(GPR_CLK), .clr(clear));
  Register #(.width(32)) reg7 (.D(w7), .en(_7), .Q(r7), .clk(GPR_CLK), .clr(clear));
  Register #(.width(32)) reg11 (.D(w11), .en(_11), .Q(r11), .clk(GPR_CLK), .clr(clear));
  Register #(.width(32)) reg15 (.D(w15), .en(_15), .Q(r15), .clk(GPR_CLK), .clr(clear));
  Register #(.width(32)) reg16 (.D(w16), .en(_16), .Q(r16), .clk(GPR_CLK), .clr(clear));
  Register #(.width(32)) reg20 (.D(w20), .en(_20), .Q(r20), .clk(GPR_CLK), .clr(clear));
  Register #(.width(32)) reg24 (.D(w24), .en(_24), .Q(r24), .clk(GPR_CLK), .clr(clear));
  Register #(.width(32)) reg28 (.D(w28), .en(_28), .Q(r28), .clk(GPR_CLK), .clr(clear));
  Register #(.width(32)) reg17 (.D(w17), .en(_17), .Q(r17), .clk(GPR_CLK), .clr(clear));
  Register #(.width(32)) reg21 (.D(w21), .en(_21), .Q(r21), .clk(GPR_CLK), .clr(clear));
  Register #(.width(32)) reg25 (.D(w25), .en(_25), .Q(r25), .clk(GPR_CLK), .clr(clear));
  Register #(.width(32)) reg29 (.D(w29), .en(_29), .Q(r29), .clk(GPR_CLK), .clr(clear));
  Demultiplexer #(.select(5), .enable("false")) demultiplexer_2 (
    .out0(_0), .out1(_1), .out2(_2), .out3(_3), .out4(_4), .out5(_5), .out6(_6), .out7(_7), .out8(_8),
    .out9(_9), .out10(_10), .out11(_11), .out12(_12), .out13(_13), .out14(_14), .out15(_15), .out16(_16),
    .out17(_17), .out18(_18), .out19(_19), .out20(_20), .out21(_21), .out22(_22), .out23(_23), .out24(_24),
    .out25(_25), .out26(_26), .out27(_27), .out28(_28), .out29(_29), .out30(_30), .out31(_31), .in(in_7),
    .sel(address_w));
  Register #(.width(32)) reg18 (.D(w18), .en(_18), .Q(r18), .clk(GPR_CLK), .clr(clear));
  Register #(.width(32)) reg22 (.D(w22), .en(_22), .Q(r22), .clk(GPR_CLK), .clr(clear));
  Register #(.width(32)) reg26 (.D(w26), .en(_26), .Q(r26), .clk(GPR_CLK), .clr(clear));
  Register #(.width(32)) reg30 (.D(w30), .en(_30), .Q(r30), .clk(GPR_CLK), .clr(clear));
  Register #(.width(32)) reg19 (.D(w19), .en(_19), .Q(r19), .clk(GPR_CLK), .clr(clear));
  Register #(.width(32)) reg23 (.D(w23), .en(_23), .Q(r23), .clk(GPR_CLK), .clr(clear));
  Register #(.width(32)) reg27 (.D(w27), .en(_27), .Q(r27), .clk(GPR_CLK), .clr(clear));
  Register #(.width(32)) reg31 (.D(w31), .en(_31), .Q(r31), .clk(GPR_CLK), .clr(clear));

  // Other names for the same wires on the sheet: add_rs[4:0] = address_rs; add_rt[4:0] = address_rt;
  //   add_w[4:0] = address_w; en0 = GPR_CLK; en1 = GPR_CLK; en2 = GPR_CLK; en3 = GPR_CLK; en4 = GPR_CLK;
  //   en5 = GPR_CLK; en6 = GPR_CLK; en7 = GPR_CLK; en8 = GPR_CLK; en9 = GPR_CLK; en10 = GPR_CLK; en11 = GPR_CLK;
  //   en12 = GPR_CLK; en13 = GPR_CLK; en14 = GPR_CLK; en15 = GPR_CLK; en16 = GPR_CLK; en17 = GPR_CLK; en18 = GPR_CLK;
  //   en19 = GPR_CLK; en20 = GPR_CLK; en21 = GPR_CLK; en22 = GPR_CLK; en23 = GPR_CLK; en24 = GPR_CLK; en25 = GPR_CLK;
  //   en26 = GPR_CLK; en27 = GPR_CLK; en28 = GPR_CLK; en29 = GPR_CLK; en30 = GPR_CLK; en31 = GPR_CLK; rst0 = clear;
  //   rst1 = clear; rst2 = clear; rst3 = clear; rst4 = clear; rst5 = clear; rst6 = clear; rst7 = clear; rst8 = clear;
  //   rst9 = clear; rst10 = clear; rst11 = clear; rst12 = clear; rst13 = clear; rst14 = clear; rst15 = clear;
  //   rst16 = clear; rst17 = clear; rst18 = clear; rst19 = clear; rst20 = clear; rst21 = clear; rst22 = clear;
  //   rst23 = clear; rst24 = clear; rst25 = clear; rst26 = clear; rst27 = clear; rst28 = clear; rst29 = clear;
  //   rst30 = clear; rst31 = clear

  // Notes on the sheet:
  //   rs输出
  //   rt输出
  //   写输入
  //   时钟信号
  //   复位信号
  //   两个读地址，一个写地址
  //   写使能
endmodule

// ALU
module \算术逻辑单元  (
  input  [31:0] A,
  input  [31:0] B,
  input  [1:0] ALU_ctr,
  output [31:0] ALUout
);

  wire [31:0] A_add, A_or, A_sub, B_, B_add, B_or, B_sub, demultiplexer_1_out3, or_1_out, shifter_1_out,
       subtractor_1_out, \组间组内全并行加法器_1_out ;

  Demultiplexer #(.select(2), .width(32), .enable("false")) demultiplexer_1 (
    .out0(A_add), .out1(A_sub), .out2(A_or), .out3(demultiplexer_1_out3), .in(A), .sel(ALU_ctr));
  Demultiplexer #(.select(2), .width(32)) demultiplexer_2 (
    .out0(B_add), .out1(B_sub), .out2(B_or), .out3(B_), .in(B), .sel(ALU_ctr));  // open: en
  \组间组内全并行加法器  \u_组间组内全并行加法器_1  (.A(A_add), .B(B_add), .OUT(\组间组内全并行加法器_1_out ));
  Subtractor #(.width(32)) subtractor_1 (.a(A_sub), .b(B_sub), .out(subtractor_1_out));  // open: bin, bout
  assign or_1_out = A_or | B_or;  // OR_Gate or_1, 32 bits wide
  Shifter #(.width(32)) shifter_1 (.in(B_), .\dist (5'b10000), .out(shifter_1_out));
  Multiplexer #(.select(2), .width(32), .enable("false")) multiplexer_1 (
    .in0(\组间组内全并行加法器_1_out ), .in1(subtractor_1_out), .in2(or_1_out), .in3(shifter_1_out), .out(ALUout),
    .sel(ALU_ctr));

  // Other names for the same wires on the sheet: sel[1:0] = ALU_ctr
endmodule

// DM
module \数据存储器  (
  input  [7:0] address,
  input  [31:0] data_in,
  input  clk,
  input  MenWr,
  input  clear,
  output [31:0] data_out
);

  wire r_en;

  not not_1 (r_en, MenWr);
  RAM #(.bus("separate")) ram_1 (
    .addr(address), .din(data_in[31:24]), .data(data_out[31:24]), .str(MenWr), .sel(1'b1), .clk(clk),
    .ld(r_en), .clr(clear));
  RAM #(.bus("separate")) ram_2 (
    .addr(address), .din(data_in[23:16]), .data(data_out[23:16]), .str(MenWr), .sel(1'b1), .clk(clk),
    .ld(r_en), .clr(clear));
  RAM #(.bus("separate")) ram_3 (
    .addr(address), .din(data_in[15:8]), .data(data_out[15:8]), .str(MenWr), .sel(1'b1), .clk(clk),
    .ld(r_en), .clr(clear));
  RAM #(.bus("separate")) ram_4 (
    .addr(address), .din(data_in[7:0]), .data(data_out[7:0]), .str(MenWr), .sel(1'b1), .clk(clk), .ld(r_en),
    .clr(clear));

  // Other names for the same wires on the sheet: data_0_7[7:0] = data_in[7:0]; data_8_15[7:0] = data_in[15:8];
  //   data_16_23[7:0] = data_in[23:16]; data_24_31[7:0] = data_in[31:24]; w_en = MenWr

  // Notes on the sheet:
  //   DM4
  //   DM3
  //   DM2
  //   DM1
endmodule

// EXT
module \扩展单元  (
  input  [15:0] data_in,
  input  Extop,
  output [31:0] data_out
);

  wire [15:0] demultiplexer_1_out0, demultiplexer_1_out1;
  wire [31:0] bit_extender_1_out, bit_extender_2_out;

  Demultiplexer #(.width(16), .enable("false")) demultiplexer_1 (
    .out0(demultiplexer_1_out0), .out1(demultiplexer_1_out1), .in(data_in), .sel(Extop));
  assign bit_extender_1_out = {{16{1'b0}}, demultiplexer_1_out0};  // Bit_Extender bit_extender_1
  assign bit_extender_2_out = {{16{demultiplexer_1_out1[15]}}, demultiplexer_1_out1};  // Bit_Extender bit_extender_2
  Multiplexer #(.width(32), .enable("false")) multiplexer_1 (
    .in0(bit_extender_1_out), .in1(bit_extender_2_out), .out(data_out), .sel(Extop));
endmodule

module \组间组内全并行加法器  (
  input  [31:0] A,
  input  [31:0] B,
  output [31:0] OUT
);

  wire C4, C8, C12, C16, C20, C24, C28, C32, G0, G1, G2, G3, G4, G5, G6, G7, G8, G9, G10, G11, G12, G13, G14,
       G15, G16, G17, G18, G19, G20, G21, G22, G23, G24, G25, G26, G27, G28, G29, G30, G31, P0, P1, P2, P3,
       P4, P5, P6, P7, P8, P9, P10, P11, P12, P13, P14, P15, P16, P17, P18, P19, P20, P21, P22, P23, P24,
       P25, P26, P27, P28, P29, P30, P31, \并行进位4位并行加法器_1_out_14 , \并行进位4位并行加法器_1_out_15 ,
       \并行进位4位并行加法器_2_out_14 , \并行进位4位并行加法器_2_out_15 , \并行进位4位并行加法器_3_out_14 , \并行进位4位并行加法器_3_out_15 ,
       \并行进位4位并行加法器_4_out_14 , \并行进位4位并行加法器_4_out_15 , \并行进位4位并行加法器_5_out_14 , \并行进位4位并行加法器_5_out_15 ,
       \并行进位4位并行加法器_6_out_14 , \并行进位4位并行加法器_6_out_15 , \并行进位4位并行加法器_7_out_14 , \并行进位4位并行加法器_7_out_15 ,
       \并行进位4位并行加法器_8_out_14 , \并行进位4位并行加法器_8_out_15 ;

  \并行进位4位并行加法器  \u_并行进位4位并行加法器_1  (
    .in_1(G31), .in_2(P31), .in_3(G30), .in_4(P30), .in_5(G29), .in_6(P29), .in_7(G28), .in_8(P28),
    .in_9(C28), .out_11(OUT[30]), .out_12(OUT[29]), .out_13(OUT[28]), .out_14(\并行进位4位并行加法器_1_out_14 ),
    .out_15(\并行进位4位并行加法器_1_out_15 ), .out_10(OUT[31]));
  \并行进位4位并行加法器  \u_并行进位4位并行加法器_2  (
    .in_1(G15), .in_2(P15), .in_3(G14), .in_4(P14), .in_5(G13), .in_6(P13), .in_7(G12), .in_8(P12),
    .in_9(C12), .out_11(OUT[14]), .out_12(OUT[13]), .out_13(OUT[12]), .out_14(\并行进位4位并行加法器_2_out_14 ),
    .out_15(\并行进位4位并行加法器_2_out_15 ), .out_10(OUT[15]));
  assign {G31, G30, G29, G28, G27, G26, G25, G24, G23, G22, G21, G20, G19, G18, G17, G16, G15, G14, G13, G12, G11, G10, G9, G8, G7, G6, G5, G4, G3, G2, G1, G0} = A & B;  // AND_Gate and_1, 32 bits wide
  assign {P31, P30, P29, P28, P27, P26, P25, P24, P23, P22, P21, P20, P19, P18, P17, P16, P15, P14, P13, P12, P11, P10, P9, P8, P7, P6, P5, P4, P3, P2, P1, P0} = A ^ B;  // XOR_Gate xor_1, 32 bits wide
  \并行进位4位并行加法器  \u_并行进位4位并行加法器_3  (
    .in_1(G27), .in_2(P27), .in_3(G26), .in_4(P26), .in_5(G25), .in_6(P25), .in_7(G24), .in_8(P24),
    .in_9(C24), .out_11(OUT[26]), .out_12(OUT[25]), .out_13(OUT[24]), .out_14(\并行进位4位并行加法器_3_out_14 ),
    .out_15(\并行进位4位并行加法器_3_out_15 ), .out_10(OUT[27]));
  \并行进位4位并行加法器  \u_并行进位4位并行加法器_4  (
    .in_1(G11), .in_2(P11), .in_3(G10), .in_4(P10), .in_5(G9), .in_6(P9), .in_7(G8), .in_8(P8), .in_9(C8),
    .out_11(OUT[10]), .out_12(OUT[9]), .out_13(OUT[8]), .out_14(\并行进位4位并行加法器_4_out_14 ),
    .out_15(\并行进位4位并行加法器_4_out_15 ), .out_10(OUT[11]));
  \组间并行进位链  \u_组间并行进位链_1  (
    .out_10(C32), .out_11(C28), .out_12(C24), .out_13(C20), .G_3(\并行进位4位并行加法器_1_out_14 ),
    .P_3(\并行进位4位并行加法器_1_out_15 ), .G_2(\并行进位4位并行加法器_3_out_14 ), .P_2(\并行进位4位并行加法器_3_out_15 ),
    .G_1(\并行进位4位并行加法器_5_out_14 ), .P_1(\并行进位4位并行加法器_5_out_15 ), .G_0(\并行进位4位并行加法器_7_out_14 ),
    .P_0(\并行进位4位并行加法器_7_out_15 ), .cin(C16));
  \组间并行进位链  \u_组间并行进位链_2  (
    .out_10(C16), .out_11(C12), .out_12(C8), .out_13(C4), .G_3(\并行进位4位并行加法器_2_out_14 ),
    .P_3(\并行进位4位并行加法器_2_out_15 ), .G_2(\并行进位4位并行加法器_4_out_14 ), .P_2(\并行进位4位并行加法器_4_out_15 ),
    .G_1(\并行进位4位并行加法器_6_out_14 ), .P_1(\并行进位4位并行加法器_6_out_15 ), .G_0(\并行进位4位并行加法器_8_out_14 ),
    .P_0(\并行进位4位并行加法器_8_out_15 ), .cin(1'b0));
  \并行进位4位并行加法器  \u_并行进位4位并行加法器_5  (
    .in_1(G23), .in_2(P23), .in_3(G22), .in_4(P22), .in_5(G21), .in_6(P21), .in_7(G20), .in_8(P20),
    .in_9(C20), .out_11(OUT[22]), .out_12(OUT[21]), .out_13(OUT[20]), .out_14(\并行进位4位并行加法器_5_out_14 ),
    .out_15(\并行进位4位并行加法器_5_out_15 ), .out_10(OUT[23]));
  \并行进位4位并行加法器  \u_并行进位4位并行加法器_6  (
    .in_1(G7), .in_2(P7), .in_3(G6), .in_4(P6), .in_5(G5), .in_6(P5), .in_7(G4), .in_8(P4), .in_9(C4),
    .out_11(OUT[6]), .out_12(OUT[5]), .out_13(OUT[4]), .out_14(\并行进位4位并行加法器_6_out_14 ),
    .out_15(\并行进位4位并行加法器_6_out_15 ), .out_10(OUT[7]));
  \并行进位4位并行加法器  \u_并行进位4位并行加法器_7  (
    .in_1(G19), .in_2(P19), .in_3(G18), .in_4(P18), .in_5(G17), .in_6(P17), .in_7(G16), .in_8(P16),
    .in_9(C16), .out_11(OUT[18]), .out_12(OUT[17]), .out_13(OUT[16]), .out_14(\并行进位4位并行加法器_7_out_14 ),
    .out_15(\并行进位4位并行加法器_7_out_15 ), .out_10(OUT[19]));
  \并行进位4位并行加法器  \u_并行进位4位并行加法器_8  (
    .in_1(G3), .in_2(P3), .in_3(G2), .in_4(P2), .in_5(G1), .in_6(P1), .in_7(G0), .in_8(P0), .in_9(1'b0),
    .out_11(OUT[2]), .out_12(OUT[1]), .out_13(OUT[0]), .out_14(\并行进位4位并行加法器_8_out_14 ),
    .out_15(\并行进位4位并行加法器_8_out_15 ), .out_10(OUT[3]));

  // Other names for the same wires on the sheet: S_0_3[3:0] = OUT[3:0]; S_4_7[3:0] = OUT[7:4];
  //   S_8_11[3:0] = OUT[11:8]; S_12_15[3:0] = OUT[15:12]; S_16_19[3:0] = OUT[19:16]; S_20_23[3:0] = OUT[23:20];
  //   S_24_27[3:0] = OUT[27:24]; S_28_31[3:0] = OUT[31:28]
endmodule

module \并行进位4位并行加法器  (
  input  in_1,
  input  in_2,
  input  in_3,
  input  in_4,
  input  in_5,
  input  in_6,
  input  in_7,
  input  in_8,
  input  in_9,
  output out_10,
  output out_11,
  output out_12,
  output out_13,
  output out_14,
  output out_15
);

  wire and_2_out, and_3_out, and_4_out, and_5_out, and_6_out, and_7_out, and_8_out, and_9_out, and_10_out,
       or_2_out, or_3_out, or_4_out;

  and and_1 (out_15, in_2, in_4, in_6, in_9);
  or or_1 (out_14, in_1, and_2_out, and_3_out, and_4_out);
  and and_2 (and_2_out, in_2, in_3);
  and and_3 (and_3_out, in_2, in_4, in_5);
  and and_4 (and_4_out, in_2, in_3, in_6, in_7);
  xor xor_1 (out_10, in_2, or_2_out);
  or or_2 (or_2_out, in_3, and_6_out, and_5_out, and_7_out);
  and and_5 (and_5_out, in_4, in_6, in_7);
  and and_6 (and_6_out, in_4, in_5);
  and and_7 (and_7_out, in_4, in_6, in_8, in_9);
  xor xor_2 (out_11, in_4, or_3_out);
  or or_3 (or_3_out, in_5, and_8_out, and_9_out);
  and and_8 (and_8_out, in_6, in_7);
  and and_9 (and_9_out, in_9, in_6, in_8);
  xor xor_3 (out_12, in_6, or_4_out);
  or or_4 (or_4_out, in_7, and_10_out);
  and and_10 (and_10_out, in_8, in_9);
  xor xor_4 (out_13, in_8, in_9);

  // Other names for the same wires on the sheet: Cin = in_9; G = in_5; G0 = in_7; G2 = in_3; G3 = in_1;
  //   G_star = out_14; P0 = in_8; P1 = in_6; P2 = in_4; P3 = in_2; P_star = out_15; S0 = out_13; S1 = out_12;
  //   S2 = out_11; S3 = out_10
endmodule

module \组间并行进位链  (
  input  G_3,
  input  P_3,
  input  G_2,
  input  P_2,
  input  G_1,
  input  P_1,
  input  G_0,
  input  P_0,
  input  cin,
  output out_10,
  output out_11,
  output out_12,
  output out_13
);

  wire and_1_out, and_2_out, and_3_out, and_5_out, and_6_out, and_7_out, and_8_out, and_9_out, and_10_out,
       and_11_out, or_1_out;

  or or_1 (or_1_out, G_3, and_2_out, and_1_out, and_3_out);
  and and_1 (and_1_out, P_3, P_2, G_1);
  and and_2 (and_2_out, P_3, G_2);
  and and_3 (and_3_out, P_3, P_2, P_1, G_0);
  and and_4 (out_10, or_1_out, and_5_out);
  and and_5 (and_5_out, P_3, P_2, P_1, P_0, cin);
  and and_6 (and_6_out, P_2, G_1);
  or or_2 (out_11, G_2, and_6_out, and_7_out, and_8_out);
  and and_7 (and_7_out, P_2, P_1, G_0);
  and and_8 (and_8_out, P_2, P_1, P_0, cin);
  or or_3 (out_12, G_1, and_9_out, and_10_out);
  and and_9 (and_9_out, P_1, G_0);
  and and_10 (and_10_out, P_1, P_0, cin);
  or or_4 (out_13, G_0, and_11_out);
  and and_11 (and_11_out, P_0, cin);
endmodule

// spilter
module \分线器  (
  input  [31:0] in_1,
  output [5:0] OPCODE,
  output [4:0] RS,
  output [4:0] RT,
  output [4:0] RD,
  output [4:0] SHAMT,
  output [5:0] FUNCT,
  output [15:0] IMM,
  output [25:0] ADDRRSS
);


  assign ADDRRSS = in_1[25:0];
  assign FUNCT = in_1[5:0];
  assign IMM = in_1[15:0];
  assign OPCODE = in_1[31:26];
  assign RD = in_1[15:11];
  assign RS = in_1[25:21];
  assign RT = in_1[20:16];
  assign SHAMT = in_1[10:6];
endmodule
